// Logisim project Chameleon CPU.circ as structural Verilog: 1 circuit, main circuit main
// RS
module main (
  input  in_1,
  input  in_2,
  input  in_3,
  input  in_4,
  input  in_5,
  input  in_6,
  input  in_7,
  input  in_8,
  input  in_9
);

  wire A1I_out, A1O_out, A2I_out, ADC_out, ADD_out, ADR_out, ALA_out, ALI_out, ALM_out, ALS_out, and_1_out,
       and_2_out, and_3_out, and_4_out, and_5_out, and_6_out, and_7_out, and_8_out, and_9_out, and_10_out,
       and_11_out, and_12_out, and_13_out, and_14_out, and_15_out, and_16_out, and_17_out, and_18_out,
       and_19_out, AND_20_out, and_21_out, and_22_out, and_23_out, and_24_out, and_25_out, and_26_out,
       and_27_out, and_28_out, and_29_out, and_30_out, and_31_out, and_32_out, and_33_out, and_34_out,
       and_35_out, and_36_out, and_37_out, and_38_out, and_39_out, and_40_out, and_41_out, and_42_out,
       and_43_out, and_44_out, and_45_out, and_46_out, and_47_out, and_48_out, and_49_out, and_50_out,
       and_51_out, and_52_out, and_53_out, and_54_out, and_55_out, and_56_out, and_57_out, and_58_out,
       and_59_out, and_60_out, and_61_out, and_62_out, and_63_out, and_64_out, and_65_out, and_66_out,
       and_67_out, and_68_out, and_69_out, and_70_out, and_71_out, and_72_out, and_73_out, and_74_out,
       and_75_out, and_76_out, and_77_out, and_78_out, and_79_out, and_80_out, and_81_out, and_82_out,
       and_83_out, and_84_out, and_85_out, and_86_out, and_87_out, and_88_out, and_89_out, and_90_out,
       and_91_out, and_92_out, and_93_out, and_94_out, and_95_out, and_96_out, and_97_out, and_98_out,
       and_99_out, and_100_out, and_101_out, and_102_out, and_103_out, and_104_out, and_105_out, and_106_out,
       and_107_out, and_108_out, and_109_out, and_110_out, and_111_out, and_112_out, and_113_out,
       and_114_out, and_115_out, and_116_out, and_117_out, and_118_out, and_119_out, and_120_out,
       and_121_out, and_122_out, and_123_out, and_124_out, and_125_out, and_126_out, and_127_out,
       and_128_out, and_129_out, and_130_out, and_131_out, and_132_out, and_133_out, and_134_out,
       and_135_out, and_136_out, and_137_out, and_138_out, and_139_out, and_140_out, and_141_out,
       and_142_out, and_143_out, and_144_out, and_145_out, and_146_out, and_147_out, and_148_out,
       and_149_out, and_150_out, and_151_out, and_152_out, and_153_out, and_154_out, and_155_out,
       and_156_out, and_157_out, and_158_out, and_159_out, and_160_out, and_161_out, and_162_out,
       and_163_out, and_164_out, and_165_out, and_166_out, and_167_out, and_168_out, and_169_out,
       and_170_out, and_171_out, and_172_out, and_173_out, and_174_out, and_175_out, and_176_out,
       and_177_out, and_178_out, and_179_out, and_180_out, and_181_out, and_182_out, and_183_out,
       and_184_out, and_185_out, and_186_out, and_187_out, and_188_out, and_189_out, and_190_out,
       and_191_out, and_192_out, and_193_out, and_194_out, and_195_out, and_196_out, and_197_out,
       and_198_out, and_199_out, and_200_out, and_201_out, and_202_out, and_203_out, and_204_out,
       and_205_out, and_206_out, and_207_out, and_208_out, and_209_out, and_210_out, and_211_out,
       and_212_out, and_213_out, and_214_out, and_215_out, and_216_out, and_217_out, and_218_out,
       and_219_out, and_220_out, and_221_out, and_222_out, and_223_out, and_224_out, and_225_out,
       and_226_out, and_227_out, and_228_out, and_229_out, and_230_out, and_231_out, and_232_out,
       and_233_out, and_234_out, and_235_out, and_236_out, and_237_out, and_238_out, and_239_out,
       and_240_out, and_241_out, and_242_out, and_243_out, and_244_out, and_245_out, and_246_out,
       and_247_out, and_248_out, and_249_out, and_250_out, and_251_out, and_252_out, and_253_out,
       and_254_out, and_255_out, and_256_out, and_257_out, and_258_out, and_259_out, and_260_out,
       and_261_out, and_262_out, and_263_out, and_264_out, and_265_out, and_266_out, and_267_out,
       and_268_out, and_269_out, and_270_out, and_271_out, and_272_out, and_273_out, and_274_out,
       and_275_out, and_276_out, and_277_out, and_278_out, and_279_out, and_280_out, and_281_out,
       and_282_out, and_283_out, and_284_out, and_285_out, and_286_out, and_287_out, and_288_out, ARI_out,
       ARO_out, ASR_out, BN_out, BR_out, CE_out, clock_1_out, comparator_1_eq, comparator_2_eq, EA_out,
       FRI_out, HC_out, HLT_out, HRD_RST_out, IB_out, IRI_out, JMP_out, JSR_out, LC_out, LDI_out, LOD_2_out,
       LOD_out, LS_out, LSL_out, LSR_out, nand_1_out, nand_2_out, nand_3_out, nand_4_out, nand_5_out,
       nand_6_out, nand_7_out, nand_8_out, NOP_out, nor_1_out, nor_2_out, nor_3_out, nor_4_out, nor_5_out,
       nor_6_out, nor_7_out, nor_8_out, nor_9_out, nor_10_out, nor_11_out, nor_12_out, nor_13_out,
       nor_14_out, nor_15_out, nor_16_out, nor_17_out, nor_18_out, nor_19_out, nor_20_out, nor_21_out,
       nor_22_out, nor_23_out, nor_24_out, nor_25_out, nor_26_out, nor_27_out, nor_28_out, nor_29_out,
       nor_30_out, nor_31_out, nor_32_out, nor_33_out, nor_34_out, nor_35_out, nor_36_out, nor_37_out,
       nor_38_out, nor_39_out, nor_40_out, nor_41_out, nor_42_out, nor_43_out, nor_44_out, nor_45_out,
       nor_46_out, nor_47_out, nor_48_out, nor_49_out, nor_50_out, nor_51_out, nor_52_out, nor_53_out,
       nor_54_out, nor_55_out, nor_56_out, nor_57_out, nor_58_out, nor_59_out, nor_60_out, nor_61_out,
       nor_62_out, nor_63_out, nor_64_out, nor_65_out, nor_66_out, nor_67_out, nor_68_out, nor_69_out,
       nor_70_out, nor_71_out, nor_72_out, nor_73_out, nor_74_out, nor_75_out, nor_76_out, nor_77_out,
       nor_78_out, nor_79_out, nor_80_out, nor_81_out, nor_82_out, nor_83_out, nor_84_out, nor_85_out,
       nor_86_out, nor_87_out, nor_88_out, nor_89_out, nor_90_out, nor_91_out, nor_92_out, nor_93_out,
       nor_94_out, nor_95_out, nor_96_out, nor_97_out, nor_98_out, nor_99_out, nor_100_out, nor_101_out,
       nor_102_out, nor_103_out, nor_104_out, nor_105_out, nor_106_out, nor_107_out, nor_108_out,
       nor_109_out, nor_110_out, nor_111_out, nor_112_out, nor_113_out, nor_114_out, nor_115_out,
       nor_116_out, nor_117_out, nor_118_out, nor_119_out, nor_120_out, nor_121_out, nor_122_out,
       nor_123_out, nor_124_out, nor_125_out, nor_126_out, nor_127_out, nor_128_out, nor_129_out,
       nor_130_out, nor_131_out, nor_132_out, nor_133_out, nor_134_out, nor_135_out, nor_136_out,
       nor_137_out, nor_138_out, nor_139_out, nor_140_out, nor_141_out, nor_142_out, nor_143_out,
       nor_144_out, nor_145_out, nor_146_out, nor_147_out, nor_148_out, nor_149_out, nor_150_out,
       nor_151_out, nor_152_out, nor_153_out, nor_154_out, nor_155_out, nor_156_out, nor_157_out,
       nor_158_out, nor_159_out, nor_160_out, nor_161_out, nor_162_out, nor_163_out, nor_164_out,
       nor_165_out, nor_166_out, nor_167_out, nor_168_out, nor_169_out, nor_170_out, nor_171_out,
       nor_172_out, nor_173_out, nor_174_out, nor_175_out, nor_176_out, nor_177_out, nor_178_out,
       nor_179_out, nor_180_out, nor_181_out, nor_182_out, nor_183_out, nor_184_out, nor_185_out,
       nor_186_out, nor_187_out, nor_188_out, nor_189_out, nor_190_out, nor_191_out, nor_192_out,
       nor_193_out, nor_194_out, nor_195_out, nor_196_out, nor_197_out, nor_198_out, nor_199_out,
       nor_200_out, nor_201_out, nor_202_out, nor_203_out, nor_204_out, nor_205_out, nor_206_out,
       nor_207_out, nor_208_out, nor_209_out, nor_210_out, nor_211_out, nor_212_out, nor_213_out,
       nor_214_out, nor_215_out, nor_216_out, nor_217_out, nor_218_out, nor_219_out, nor_220_out,
       nor_221_out, nor_222_out, nor_223_out, nor_224_out, nor_225_out, nor_226_out, nor_227_out,
       nor_228_out, nor_229_out, nor_230_out, nor_231_out, nor_232_out, nor_233_out, nor_234_out,
       nor_235_out, nor_236_out, nor_237_out, nor_238_out, nor_239_out, nor_240_out, nor_241_out,
       nor_242_out, nor_243_out, nor_244_out, nor_245_out, nor_246_out, nor_247_out, nor_248_out,
       nor_249_out, nor_250_out, nor_251_out, nor_252_out, nor_253_out, nor_254_out, nor_255_out,
       nor_256_out, nor_257_out, nor_258_out, nor_259_out, nor_260_out, nor_261_out, nor_262_out,
       nor_263_out, nor_264_out, nor_265_out, nor_266_out, nor_267_out, nor_268_out, nor_269_out,
       nor_270_out, nor_271_out, nor_272_out, nor_273_out, nor_274_out, nor_275_out, nor_276_out,
       nor_277_out, nor_278_out, nor_279_out, nor_280_out, nor_281_out, nor_282_out, nor_283_out,
       nor_284_out, nor_285_out, nor_286_out, nor_287_out, nor_288_out, nor_289_out, nor_290_out,
       nor_291_out, nor_292_out, nor_293_out, nor_294_out, nor_295_out, nor_296_out, nor_297_out,
       nor_298_out, nor_299_out, nor_300_out, nor_301_out, nor_302_out, nor_303_out, nor_304_out,
       nor_305_out, nor_306_out, nor_307_out, nor_308_out, nor_309_out, nor_310_out, nor_311_out,
       nor_312_out, nor_313_out, nor_314_out, nor_315_out, nor_316_out, nor_317_out, nor_318_out,
       nor_319_out, nor_320_out, nor_321_out, nor_322_out, nor_323_out, nor_324_out, nor_325_out,
       nor_326_out, nor_327_out, nor_328_out, nor_329_out, nor_330_out, nor_331_out, nor_332_out,
       nor_333_out, nor_334_out, nor_335_out, nor_336_out, nor_337_out, nor_338_out, nor_339_out,
       nor_340_out, nor_341_out, nor_342_out, nor_343_out, nor_344_out, nor_345_out, nor_346_out,
       nor_347_out, nor_348_out, nor_349_out, nor_350_out, nor_351_out, nor_352_out, nor_353_out,
       nor_354_out, nor_355_out, nor_356_out, nor_357_out, nor_358_out, nor_359_out, nor_360_out,
       nor_361_out, nor_362_out, nor_363_out, nor_364_out, nor_365_out, nor_366_out, nor_367_out,
       nor_368_out, nor_369_out, nor_370_out, nor_371_out, nor_372_out, nor_373_out, nor_374_out,
       nor_375_out, nor_376_out, nor_377_out, nor_378_out, nor_379_out, nor_380_out, nor_381_out,
       nor_382_out, nor_383_out, nor_384_out, nor_385_out, nor_386_out, nor_387_out, nor_388_out,
       nor_389_out, nor_390_out, nor_391_out, nor_392_out, nor_393_out, nor_394_out, nor_395_out,
       nor_396_out, nor_397_out, nor_398_out, nor_399_out, nor_400_out, nor_401_out, nor_402_out,
       nor_403_out, nor_404_out, nor_405_out, nor_406_out, nor_407_out, nor_408_out, nor_409_out,
       nor_410_out, nor_411_out, nor_412_out, nor_413_out, nor_414_out, nor_415_out, nor_416_out,
       nor_417_out, nor_418_out, nor_419_out, nor_420_out, nor_421_out, nor_422_out, nor_423_out,
       nor_424_out, nor_425_out, nor_426_out, nor_427_out, nor_428_out, nor_429_out, nor_430_out,
       nor_431_out, nor_432_out, nor_433_out, nor_434_out, nor_435_out, nor_436_out, nor_437_out,
       nor_438_out, nor_439_out, nor_440_out, nor_441_out, nor_442_out, nor_443_out, nor_444_out,
       nor_445_out, nor_446_out, nor_447_out, nor_448_out, nor_449_out, nor_450_out, nor_451_out,
       nor_452_out, nor_453_out, nor_454_out, nor_455_out, nor_456_out, nor_457_out, nor_458_out,
       nor_459_out, nor_460_out, nor_461_out, nor_462_out, nor_463_out, nor_464_out, nor_465_out,
       nor_466_out, nor_467_out, nor_468_out, nor_469_out, nor_470_out, nor_471_out, nor_472_out,
       nor_473_out, not_1_out, not_2_out, not_3_out, not_4_out, not_5_out, not_6_out, not_7_out, not_8_out,
       not_9_out, ONC_out, or_1_out, OR_2_out, or_3_out, or_4_out, or_5_out, or_6_out, or_7_out, or_8_out,
       or_9_out, or_10_out, or_11_out, or_12_out, or_13_out, or_14_out, or_15_out, or_16_out, or_17_out,
       or_18_out, or_19_out, or_20_out, or_21_out, or_22_out, or_23_out, or_24_out, or_25_out, P1I_out,
       P1O_out, P2I_out, P2O_out, PCI_out, POP_out, PRC_out, PSH_out, RC_out, RCL_out, RCR_out, RD_out,
       ROL_out, ROR_out, RS_out, RSR_out, RST_out, SBB_out, SFT_RST_out, STD_out, STI_out, STO_out, STP_out,
       SUB_out, TWC_out, WR_out, X1_out, X2_out, X3_out, xnor_1_out, xnor_2_out, xnor_3_out, xnor_4_out,
       xnor_5_out, xnor_6_out, xnor_7_out, xnor_8_out, xnor_9_out, xnor_10_out, xnor_11_out, xnor_12_out,
       xnor_13_out, xnor_14_out, xnor_15_out, xnor_16_out, xnor_17_out, xnor_18_out, xnor_19_out,
       xnor_20_out, xnor_21_out, xnor_22_out, xnor_23_out, xnor_24_out, xnor_25_out, xnor_26_out,
       xnor_27_out, xnor_28_out, xnor_29_out, xnor_30_out, xnor_31_out, xnor_32_out, xnor_33_out,
       xnor_34_out, xnor_35_out, xnor_36_out, xnor_37_out, xnor_38_out, xnor_39_out, xnor_40_out,
       xnor_41_out, xor_2_out, XOR_out;
  wire [7:0] keyboard_1_data;
  wire [15:0] OC_9_out;

  Pull_Resistor #(.pull(1)) pull_resistor_1 (.node(in_9));
  Pull_Resistor #(.pull(1)) pull_resistor_2 (.node(in_4));
  Pull_Resistor #(.pull(1)) pull_resistor_3 (.node(in_8));
  Pull_Resistor #(.pull(1)) pull_resistor_4 (.node(in_2));
  Pull_Resistor #(.pull(1)) pull_resistor_5 (.node(in_5));
  Pull_Resistor #(.pull(1)) pull_resistor_6 (.node(in_6));
  Pull_Resistor #(.pull(1)) pull_resistor_7 (.node(in_3));
  Pull_Resistor #(.pull(1)) pull_resistor_8 (.node(in_1));
  not not_1 (not_1_out, nor_161_out);
  not not_2 (not_2_out, nor_163_out);
  not not_3 (not_3_out, nor_165_out);
  not not_4 (not_4_out, nor_167_out);
  not not_5 (not_5_out, LOD_2_out);
  and ADD (ADD_out, not_5_out, not_4_out, not_3_out, not_2_out, not_1_out);
  and ADC (ADC_out, not_5_out, not_4_out, not_3_out, not_2_out, nor_161_out);
  or LC (LC_out, ASR_out, ROL_out);
  or CE (CE_out, ADC_out, SBB_out, RCL_out, RCR_out);
  and SUB (SUB_out, not_5_out, not_4_out, not_3_out, nor_163_out, not_1_out);
  and SBB (SBB_out, not_5_out, not_4_out, not_3_out, nor_163_out, nor_161_out);
  buf RC (RC_out, ROR_out);
  nand nand_1 (nand_1_out, EA_out, nor_77_out);
  xnor xnor_1 (xnor_1_out, IB_out, in_1);
  nand nand_2 (nand_2_out, EA_out, nor_79_out);
  xnor xnor_2 (xnor_2_out, IB_out, in_2);
  nand nand_3 (nand_3_out, EA_out, nor_81_out);
  xnor xnor_3 (xnor_3_out, IB_out, in_3);
  nand nand_4 (nand_4_out, EA_out, nor_83_out);
  xnor xnor_4 (xnor_4_out, IB_out, in_4);
  nand nand_5 (nand_5_out, EA_out, nor_85_out);
  xnor xnor_5 (xnor_5_out, IB_out, in_5);
  nand nand_6 (nand_6_out, EA_out, nor_87_out);
  xnor xnor_6 (xnor_6_out, IB_out, in_6);
  nand nand_7 (nand_7_out, EA_out, nor_89_out);
  xnor xnor_7 (xnor_7_out, IB_out, in_8);
  nand nand_8 (nand_8_out, EA_out, nor_91_out);
  xnor xnor_8 (xnor_8_out, IB_out, in_9);
  and ONC (ONC_out, not_5_out, not_4_out, nor_165_out, not_2_out, not_1_out);
  or HC (HC_out, SUB_out, TWC_out, AND_20_out, XOR_out);
  and and_1 (and_1_out, RC_out, in_1);
  and and_2 (and_2_out, LC_out, in_9);
  and and_3 (and_3_out, CE_out, nor_153_out);
  and and_4 (and_4_out, nand_1_out, X1_out, xnor_1_out);
  nor nor_1 (nor_1_out, and_4_out, nor_2_out);
  nor nor_2 (nor_2_out, nand_1_out, X2_out, xnor_1_out);
  and and_5 (and_5_out, nand_2_out, X1_out, xnor_2_out);
  nor nor_3 (nor_3_out, and_5_out, nor_4_out);
  nor nor_4 (nor_4_out, nand_2_out, X2_out, xnor_2_out);
  and and_6 (and_6_out, nand_3_out, X1_out, xnor_3_out);
  nor nor_5 (nor_5_out, and_6_out, nor_6_out);
  nor nor_6 (nor_6_out, nand_3_out, X2_out, xnor_3_out);
  and and_7 (and_7_out, nand_4_out, X1_out, xnor_4_out);
  nor nor_7 (nor_7_out, and_7_out, nor_8_out);
  nor nor_8 (nor_8_out, nand_4_out, X2_out, xnor_4_out);
  and and_8 (and_8_out, nand_5_out, X1_out, xnor_5_out);
  nor nor_9 (nor_9_out, and_8_out, nor_10_out);
  nor nor_10 (nor_10_out, nand_5_out, X2_out, xnor_5_out);
  and and_9 (and_9_out, nand_6_out, X1_out, xnor_6_out);
  nor nor_11 (nor_11_out, and_9_out, nor_12_out);
  nor nor_12 (nor_12_out, nand_6_out, X2_out, xnor_6_out);
  and and_10 (and_10_out, nand_7_out, X1_out, xnor_7_out);
  nor nor_13 (nor_13_out, and_10_out, nor_14_out);
  nor nor_14 (nor_14_out, nand_7_out, X2_out, xnor_7_out);
  and and_11 (and_11_out, nand_8_out, X1_out, xnor_8_out);
  nor nor_15 (nor_15_out, and_11_out, nor_16_out);
  nor nor_16 (nor_16_out, nand_8_out, X2_out, xnor_8_out);
  and TWC (TWC_out, not_5_out, not_4_out, nor_165_out, not_2_out, nor_161_out);
  nor EA (EA_out, ONC_out, TWC_out, LOD_2_out);
  nor IB (IB_out, LOD_2_out, ADD_out, ADC_out, AND_20_out, OR_2_out);
  or or_1 (or_1_out, HC_out, and_1_out, and_2_out, and_3_out);
  nor nor_17 (nor_17_out, or_1_out, nor_1_out);
  and and_12 (and_12_out, or_1_out, nor_1_out);
  nor nor_18 (nor_18_out, or_3_out, nor_3_out);
  and and_13 (and_13_out, or_3_out, nor_3_out);
  nor nor_19 (nor_19_out, or_4_out, nor_5_out);
  and and_14 (and_14_out, or_4_out, nor_5_out);
  nor nor_20 (nor_20_out, or_5_out, nor_7_out);
  and and_15 (and_15_out, or_5_out, nor_7_out);
  nor nor_21 (nor_21_out, or_6_out, nor_9_out);
  and and_16 (and_16_out, or_6_out, nor_9_out);
  nor nor_22 (nor_22_out, or_7_out, nor_11_out);
  and and_17 (and_17_out, or_7_out, nor_11_out);
  nor nor_23 (nor_23_out, or_8_out, nor_13_out);
  and and_18 (and_18_out, or_8_out, nor_13_out);
  nor nor_24 (nor_24_out, or_9_out, nor_15_out);
  and and_19 (and_19_out, or_9_out, nor_15_out);
  and AND_20 (AND_20_out, not_5_out, not_4_out, nor_165_out, nor_163_out, not_1_out);
  and OR_2 (OR_2_out, not_5_out, not_4_out, nor_165_out, nor_163_out, nor_161_out);
  not X1 (X1_out, AND_20_out);
  or or_3 (or_3_out, and_12_out, X3_out, nor_2_out);
  or or_4 (or_4_out, and_13_out, X3_out, nor_4_out);
  or or_5 (or_5_out, and_14_out, X3_out, nor_6_out);
  or or_6 (or_6_out, and_15_out, X3_out, nor_8_out);
  or or_7 (or_7_out, and_16_out, X3_out, nor_10_out);
  or or_8 (or_8_out, and_17_out, X3_out, nor_12_out);
  or or_9 (or_9_out, and_18_out, X3_out, nor_14_out);
  nor nor_25 (nor_25_out, and_19_out, X3_out, nor_16_out);
  and XOR (XOR_out, not_5_out, nor_167_out, not_3_out, not_2_out, not_1_out);
  buf X3 (X3_out, XOR_out);
  buf X2 (X2_out, OR_2_out);
  and and_21 (and_21_out, or_1_out, LS_out);
  nor nor_26 (nor_26_out, LS_out, nor_17_out, and_12_out, RS_out);
  and and_22 (and_22_out, RS_out, in_2);
  and and_23 (and_23_out, in_1, LS_out);
  nor nor_27 (nor_27_out, LS_out, nor_18_out, and_13_out, RS_out);
  and and_24 (and_24_out, RS_out, in_3);
  and and_25 (and_25_out, in_2, LS_out);
  nor nor_28 (nor_28_out, LS_out, nor_19_out, and_14_out, RS_out);
  and and_26 (and_26_out, RS_out, in_4);
  and and_27 (and_27_out, in_3, LS_out);
  nor nor_29 (nor_29_out, LS_out, nor_20_out, and_15_out, RS_out);
  and and_28 (and_28_out, RS_out, in_5);
  and and_29 (and_29_out, in_4, LS_out);
  nor nor_30 (nor_30_out, LS_out, nor_21_out, and_16_out, RS_out);
  and and_30 (and_30_out, RS_out, in_6);
  and and_31 (and_31_out, in_5, LS_out);
  nor nor_31 (nor_31_out, LS_out, nor_22_out, and_17_out, RS_out);
  and and_32 (and_32_out, RS_out, in_8);
  and and_33 (and_33_out, in_6, LS_out);
  nor nor_32 (nor_32_out, LS_out, nor_23_out, and_18_out, RS_out);
  and and_34 (and_34_out, RS_out, in_9);
  and and_35 (and_35_out, in_8, LS_out);
  nor nor_33 (nor_33_out, LS_out, nor_24_out, and_19_out, RS_out);
  and and_36 (and_36_out, RS_out, or_1_out);
  and and_37 (and_37_out, LS_out, in_9);
  and and_38 (and_38_out, RS_out, in_1);
  nor nor_34 (nor_34_out, LS_out, nor_25_out, RS_out);
  and LSL (LSL_out, not_5_out, nor_167_out, not_3_out, not_2_out, nor_161_out);
  or LS (LS_out, LSL_out, ROL_out, RCL_out);
  or or_10 (or_10_out, and_21_out, nor_26_out, and_22_out);
  or or_11 (or_11_out, and_23_out, nor_27_out, and_24_out);
  or or_12 (or_12_out, and_25_out, nor_28_out, and_26_out);
  or or_13 (or_13_out, and_27_out, nor_29_out, and_28_out);
  or or_14 (or_14_out, and_29_out, nor_30_out, and_30_out);
  or or_15 (or_15_out, and_31_out, nor_31_out, and_32_out);
  or or_16 (or_16_out, and_33_out, nor_32_out, and_34_out);
  or or_17 (or_17_out, and_35_out, nor_33_out, and_36_out);
  or or_18 (or_18_out, and_37_out, and_38_out, nor_34_out);
  and LSR (LSR_out, not_5_out, nor_167_out, not_3_out, nor_163_out, not_1_out);
  and ASR (ASR_out, not_5_out, nor_167_out, not_3_out, nor_163_out, nor_161_out);
  or RS (RS_out, LSR_out, ASR_out, ROR_out, RCR_out);
  nor nor_35 (nor_35_out, or_10_out, or_11_out, or_12_out, or_13_out, or_14_out, or_15_out, or_16_out, or_17_out);
  xor xor_2 (xor_2_out, or_9_out, or_18_out);
  and ROL (ROL_out, not_5_out, nor_167_out, nor_165_out, not_2_out, not_1_out);
  and ROR (ROR_out, not_5_out, nor_167_out, nor_165_out, not_2_out, nor_161_out);
  nor nor_36 (nor_36_out, nor_76_out, ARI_out);
  and and_39 (and_39_out, ARI_out, or_10_out);
  nor nor_37 (nor_37_out, nor_78_out, ARI_out);
  and and_40 (and_40_out, ARI_out, or_11_out);
  nor nor_38 (nor_38_out, nor_80_out, ARI_out);
  and and_41 (and_41_out, ARI_out, or_12_out);
  nor nor_39 (nor_39_out, nor_82_out, ARI_out);
  and and_42 (and_42_out, ARI_out, or_13_out);
  nor nor_40 (nor_40_out, nor_84_out, ARI_out);
  and and_43 (and_43_out, ARI_out, or_14_out);
  nor nor_41 (nor_41_out, nor_86_out, ARI_out);
  and and_44 (and_44_out, ARI_out, or_15_out);
  nor nor_42 (nor_42_out, nor_88_out, ARI_out);
  and and_45 (and_45_out, ARI_out, or_16_out);
  nor nor_43 (nor_43_out, nor_90_out, ARI_out);
  and and_46 (and_46_out, ARI_out, or_17_out);
  and RCL (RCL_out, not_5_out, nor_167_out, nor_165_out, nor_163_out, not_1_out);
  and RCR (RCR_out, not_5_out, nor_167_out, nor_165_out, nor_163_out, nor_161_out);
  nor nor_44 (nor_44_out, nor_36_out, and_39_out, and_157_out);
  nor nor_45 (nor_45_out, nor_44_out, and_157_out);
  nor nor_46 (nor_46_out, nor_37_out, and_40_out, and_157_out);
  nor nor_47 (nor_47_out, nor_46_out, and_157_out);
  nor nor_48 (nor_48_out, nor_38_out, and_41_out, and_157_out);
  nor nor_49 (nor_49_out, nor_48_out, and_157_out);
  nor nor_50 (nor_50_out, nor_39_out, and_42_out, and_157_out);
  nor nor_51 (nor_51_out, nor_50_out, and_157_out);
  nor nor_52 (nor_52_out, nor_40_out, and_43_out, and_157_out);
  nor nor_53 (nor_53_out, nor_52_out, and_157_out);
  nor nor_54 (nor_54_out, nor_41_out, and_44_out, and_157_out);
  nor nor_55 (nor_55_out, nor_54_out, and_157_out);
  nor nor_56 (nor_56_out, nor_42_out, and_45_out, and_157_out);
  nor nor_57 (nor_57_out, nor_56_out, and_157_out);
  nor nor_58 (nor_58_out, nor_43_out, and_46_out, and_157_out);
  nor nor_59 (nor_59_out, nor_58_out, and_157_out);
  nor nor_60 (nor_60_out, nor_44_out, nor_61_out);
  nor nor_61 (nor_61_out, nor_60_out, nor_45_out);
  nor nor_62 (nor_62_out, nor_46_out, nor_63_out);
  nor nor_63 (nor_63_out, nor_62_out, nor_47_out);
  nor nor_64 (nor_64_out, nor_48_out, nor_65_out);
  nor nor_65 (nor_65_out, nor_64_out, nor_49_out);
  nor nor_66 (nor_66_out, nor_50_out, nor_67_out);
  nor nor_67 (nor_67_out, nor_66_out, nor_51_out);
  nor nor_68 (nor_68_out, nor_52_out, nor_69_out);
  nor nor_69 (nor_69_out, nor_68_out, nor_53_out);
  nor nor_70 (nor_70_out, nor_54_out, nor_71_out);
  nor nor_71 (nor_71_out, nor_70_out, nor_55_out);
  nor nor_72 (nor_72_out, nor_56_out, nor_73_out);
  nor nor_73 (nor_73_out, nor_72_out, nor_57_out);
  nor nor_74 (nor_74_out, nor_58_out, nor_75_out);
  nor nor_75 (nor_75_out, nor_74_out, nor_59_out);
  nor nor_76 (nor_76_out, and_47_out, nor_77_out);
  and and_47 (and_47_out, nor_60_out, and_157_out);
  nor nor_77 (nor_77_out, nor_76_out, and_48_out);
  and and_48 (and_48_out, and_157_out, nor_61_out);
  and and_49 (and_49_out, nor_62_out, and_157_out);
  nor nor_78 (nor_78_out, and_49_out, nor_79_out);
  nor nor_79 (nor_79_out, nor_78_out, and_50_out);
  and and_50 (and_50_out, and_157_out, nor_63_out);
  nor nor_80 (nor_80_out, and_51_out, nor_81_out);
  and and_51 (and_51_out, nor_64_out, and_157_out);
  nor nor_81 (nor_81_out, nor_80_out, and_52_out);
  and and_52 (and_52_out, and_157_out, nor_65_out);
  nor nor_82 (nor_82_out, and_53_out, nor_83_out);
  and and_53 (and_53_out, nor_66_out, and_157_out);
  and and_54 (and_54_out, and_157_out, nor_67_out);
  nor nor_83 (nor_83_out, nor_82_out, and_54_out);
  nor nor_84 (nor_84_out, and_55_out, nor_85_out);
  and and_55 (and_55_out, nor_68_out, and_157_out);
  nor nor_85 (nor_85_out, nor_84_out, and_56_out);
  and and_56 (and_56_out, and_157_out, nor_69_out);
  nor nor_86 (nor_86_out, and_57_out, nor_87_out);
  and and_57 (and_57_out, nor_70_out, and_157_out);
  nor nor_87 (nor_87_out, nor_86_out, and_58_out);
  and and_58 (and_58_out, and_157_out, nor_71_out);
  nor nor_88 (nor_88_out, and_59_out, nor_89_out);
  and and_59 (and_59_out, nor_72_out, and_157_out);
  nor nor_89 (nor_89_out, nor_88_out, and_60_out);
  and and_60 (and_60_out, and_157_out, nor_73_out);
  nor nor_90 (nor_90_out, and_61_out, nor_91_out);
  and and_61 (and_61_out, nor_74_out, and_157_out);
  and and_62 (and_62_out, and_157_out, nor_75_out);
  nor nor_91 (nor_91_out, nor_90_out, and_62_out);
  nand OC (in_1, nor_76_out, ARO_out);
  nand OC_2 (in_2, nor_78_out, ARO_out);
  nand OC_3 (in_3, nor_80_out, ARO_out);
  nand OC_4 (in_4, nor_82_out, ARO_out);
  nand OC_5 (in_5, nor_84_out, ARO_out);
  nand OC_6 (in_6, nor_86_out, ARO_out);
  nand OC_7 (in_8, nor_88_out, ARO_out);
  nand OC_8 (in_9, nor_90_out, ARO_out);
  nor nor_92 (nor_92_out, nor_152_out, FRI_out);
  and and_63 (and_63_out, FRI_out, or_18_out);
  nor nor_93 (nor_93_out, nor_154_out, FRI_out);
  and and_64 (and_64_out, FRI_out, nor_35_out);
  nor nor_94 (nor_94_out, nor_156_out, FRI_out);
  and and_65 (and_65_out, FRI_out, or_17_out);
  nor nor_95 (nor_95_out, nor_158_out, FRI_out);
  and and_66 (and_66_out, FRI_out, xor_2_out);
  nor nor_96 (nor_96_out, nor_160_out, IRI_out);
  and and_67 (and_67_out, IRI_out, in_1);
  nor nor_97 (nor_97_out, nor_162_out, IRI_out);
  and and_68 (and_68_out, IRI_out, in_2);
  nor nor_98 (nor_98_out, nor_164_out, IRI_out);
  and and_69 (and_69_out, IRI_out, in_3);
  nor nor_99 (nor_99_out, nor_166_out, IRI_out);
  and and_70 (and_70_out, IRI_out, in_4);
  nor nor_100 (nor_100_out, nor_168_out, IRI_out);
  and and_71 (and_71_out, IRI_out, in_5);
  nor nor_101 (nor_101_out, nor_170_out, IRI_out);
  and and_72 (and_72_out, IRI_out, in_6);
  nor nor_102 (nor_102_out, nor_172_out, IRI_out);
  and and_73 (and_73_out, IRI_out, in_8);
  nor nor_103 (nor_103_out, nor_174_out, IRI_out);
  and and_74 (and_74_out, IRI_out, in_9);
  nor nor_104 (nor_104_out, nor_92_out, and_63_out, and_157_out);
  nor nor_105 (nor_105_out, nor_104_out, and_157_out);
  nor nor_106 (nor_106_out, nor_93_out, and_64_out, and_157_out);
  nor nor_107 (nor_107_out, nor_106_out, and_157_out);
  nor nor_108 (nor_108_out, nor_94_out, and_65_out, and_157_out);
  nor nor_109 (nor_109_out, nor_108_out, and_157_out);
  nor nor_110 (nor_110_out, nor_95_out, and_66_out, and_157_out);
  nor nor_111 (nor_111_out, nor_110_out, and_157_out);
  nor nor_112 (nor_112_out, nor_96_out, and_67_out, and_157_out);
  nor nor_113 (nor_113_out, nor_112_out, and_157_out);
  nor nor_114 (nor_114_out, nor_97_out, and_68_out, and_157_out);
  nor nor_115 (nor_115_out, nor_114_out, and_157_out);
  nor nor_116 (nor_116_out, nor_98_out, and_69_out, and_157_out);
  nor nor_117 (nor_117_out, nor_116_out, and_157_out);
  nor nor_118 (nor_118_out, nor_99_out, and_70_out, and_157_out);
  nor nor_119 (nor_119_out, nor_118_out, and_157_out);
  nor nor_120 (nor_120_out, nor_100_out, and_71_out, and_157_out);
  nor nor_121 (nor_121_out, nor_120_out, and_157_out);
  nor nor_122 (nor_122_out, nor_101_out, and_72_out, and_157_out);
  nor nor_123 (nor_123_out, nor_122_out, and_157_out);
  nor nor_124 (nor_124_out, nor_102_out, and_73_out, and_157_out);
  nor nor_125 (nor_125_out, nor_124_out, and_157_out);
  nor nor_126 (nor_126_out, nor_103_out, and_74_out, and_157_out);
  nor nor_127 (nor_127_out, nor_126_out, and_157_out);
  nor nor_128 (nor_128_out, nor_104_out, nor_129_out);
  nor nor_129 (nor_129_out, nor_128_out, nor_105_out);
  nor nor_130 (nor_130_out, nor_106_out, nor_131_out);
  nor nor_131 (nor_131_out, nor_130_out, nor_107_out);
  nor nor_132 (nor_132_out, nor_108_out, nor_133_out);
  nor nor_133 (nor_133_out, nor_132_out, nor_109_out);
  nor nor_134 (nor_134_out, nor_110_out, nor_135_out);
  nor nor_135 (nor_135_out, nor_134_out, nor_111_out);
  nor nor_136 (nor_136_out, nor_112_out, nor_137_out);
  nor nor_137 (nor_137_out, nor_136_out, nor_113_out);
  nor nor_138 (nor_138_out, nor_114_out, nor_139_out);
  nor nor_139 (nor_139_out, nor_138_out, nor_115_out);
  nor nor_140 (nor_140_out, nor_116_out, nor_141_out);
  nor nor_141 (nor_141_out, nor_140_out, nor_117_out);
  nor nor_142 (nor_142_out, nor_118_out, nor_143_out);
  nor nor_143 (nor_143_out, nor_142_out, nor_119_out);
  nor nor_144 (nor_144_out, nor_120_out, nor_145_out);
  nor nor_145 (nor_145_out, nor_144_out, nor_121_out);
  nor nor_146 (nor_146_out, nor_122_out, nor_147_out);
  nor nor_147 (nor_147_out, nor_146_out, nor_123_out);
  nor nor_148 (nor_148_out, nor_124_out, nor_149_out);
  nor nor_149 (nor_149_out, nor_148_out, nor_125_out);
  nor nor_150 (nor_150_out, nor_126_out, nor_151_out);
  nor nor_151 (nor_151_out, nor_150_out, nor_127_out);
  and and_75 (and_75_out, nor_128_out, and_157_out);
  and and_76 (and_76_out, and_157_out, nor_129_out);
  and and_77 (and_77_out, nor_130_out, and_157_out);
  and and_78 (and_78_out, and_157_out, nor_131_out);
  and and_79 (and_79_out, nor_132_out, and_157_out);
  and and_80 (and_80_out, and_157_out, nor_133_out);
  and and_81 (and_81_out, nor_134_out, and_157_out);
  and and_82 (and_82_out, and_157_out, nor_135_out);
  and and_83 (and_83_out, nor_136_out, and_157_out);
  and and_84 (and_84_out, and_157_out, nor_137_out);
  and and_85 (and_85_out, nor_138_out, and_157_out);
  and and_86 (and_86_out, and_157_out, nor_139_out);
  and and_87 (and_87_out, nor_140_out, and_157_out);
  and and_88 (and_88_out, and_157_out, nor_141_out);
  and and_89 (and_89_out, nor_142_out, and_157_out);
  and and_90 (and_90_out, and_157_out, nor_143_out);
  and and_91 (and_91_out, nor_144_out, and_157_out);
  and and_92 (and_92_out, and_157_out, nor_145_out);
  and and_93 (and_93_out, nor_146_out, and_157_out);
  and and_94 (and_94_out, and_157_out, nor_147_out);
  and and_95 (and_95_out, nor_148_out, and_157_out);
  and and_96 (and_96_out, and_157_out, nor_149_out);
  and and_97 (and_97_out, nor_150_out, and_157_out);
  and and_98 (and_98_out, and_157_out, nor_151_out);
  nor nor_152 (nor_152_out, and_75_out, nor_153_out);
  nor nor_153 (nor_153_out, nor_152_out, and_76_out);
  nor nor_154 (nor_154_out, and_77_out, nor_155_out);
  nor nor_155 (nor_155_out, nor_154_out, and_78_out);
  nor nor_156 (nor_156_out, and_79_out, nor_157_out);
  nor nor_157 (nor_157_out, nor_156_out, and_80_out);
  nor nor_158 (nor_158_out, and_81_out, nor_159_out);
  nor nor_159 (nor_159_out, nor_158_out, and_82_out);
  nor nor_160 (nor_160_out, and_83_out, nor_161_out);
  nor nor_161 (nor_161_out, nor_160_out, and_84_out);
  nor nor_162 (nor_162_out, and_85_out, nor_163_out);
  nor nor_163 (nor_163_out, nor_162_out, and_86_out);
  nor nor_164 (nor_164_out, and_87_out, nor_165_out);
  nor nor_165 (nor_165_out, nor_164_out, and_88_out);
  nor nor_166 (nor_166_out, and_89_out, nor_167_out);
  nor nor_167 (nor_167_out, nor_166_out, and_90_out);
  nor nor_168 (nor_168_out, and_91_out, nor_169_out);
  nor nor_169 (nor_169_out, nor_168_out, and_92_out);
  nor nor_170 (nor_170_out, and_93_out, nor_171_out);
  nor nor_171 (nor_171_out, nor_170_out, and_94_out);
  nor nor_172 (nor_172_out, and_95_out, nor_173_out);
  nor nor_173 (nor_173_out, nor_172_out, and_96_out);
  nor nor_174 (nor_174_out, and_97_out, nor_175_out);
  nor nor_175 (nor_175_out, nor_174_out, and_98_out);
  and and_99 (and_99_out, nor_152_out, BN_out, nor_161_out);
  and and_100 (and_100_out, nor_161_out, BR_out, nor_153_out);
  and and_101 (and_101_out, nor_154_out, BN_out, nor_163_out);
  and and_102 (and_102_out, nor_163_out, BR_out, nor_155_out);
  and and_103 (and_103_out, nor_156_out, BN_out, nor_165_out);
  and and_104 (and_104_out, nor_165_out, BR_out, nor_157_out);
  and and_105 (and_105_out, nor_158_out, BN_out, nor_167_out);
  and and_106 (and_106_out, nor_167_out, BR_out, nor_159_out);
  and and_107 (and_107_out, nor_176_out, or_19_out);
  or or_19 (or_19_out, BR_out, BN_out);
  and NOP (NOP_out, nor_168_out, nor_170_out, nor_172_out, nor_174_out, nor_241_out);
  and ALM (ALM_out, nor_169_out, nor_170_out, nor_172_out, nor_174_out, nor_241_out);
  and ALA (ALA_out, nor_168_out, nor_171_out, nor_172_out, nor_174_out, nor_241_out);
  and ALI (ALI_out, nor_169_out, nor_171_out, nor_172_out, nor_174_out, nor_241_out);
  and ALS (ALS_out, nor_168_out, nor_170_out, nor_173_out, nor_174_out, nor_241_out);
  and LOD (LOD_out, nor_169_out, nor_170_out, nor_173_out, nor_174_out, nor_241_out);
  and LDI (LDI_out, nor_168_out, nor_171_out, nor_173_out, nor_174_out, nor_241_out);
  and STO (STO_out, nor_169_out, nor_171_out, nor_173_out, nor_174_out, nor_241_out);
  and PSH (PSH_out, nor_168_out, nor_170_out, nor_172_out, nor_175_out, nor_241_out);
  and POP (POP_out, nor_169_out, nor_170_out, nor_172_out, nor_175_out, nor_241_out);
  and JMP (JMP_out, nor_168_out, nor_171_out, nor_172_out, nor_175_out, nor_241_out);
  and BR (BR_out, nor_169_out, nor_171_out, nor_172_out, nor_175_out, nor_241_out);
  and BN (BN_out, nor_168_out, nor_170_out, nor_173_out, nor_175_out, nor_241_out);
  and JSR (JSR_out, nor_169_out, nor_170_out, nor_173_out, nor_175_out, nor_241_out);
  and RSR (RSR_out, nor_168_out, nor_171_out, nor_173_out, nor_175_out, nor_241_out);
  and HLT (HLT_out, nor_169_out, nor_171_out, nor_173_out, nor_175_out, nor_241_out);
  nor nor_176 (nor_176_out, and_99_out, and_100_out, and_101_out, and_102_out, and_103_out, and_104_out, and_105_out, and_106_out);
  not not_6 (not_6_out, nor_176_out);
  nor nor_177 (nor_177_out, nor_193_out, RST_out);
  nor nor_178 (nor_178_out, xnor_9_out, RST_out);
  nor nor_179 (nor_179_out, xnor_10_out, RST_out);
  or or_20 (or_20_out, ALM_out, LOD_out, STO_out);
  or or_21 (or_21_out, and_107_out, NOP_out);
  and and_108 (and_108_out, or_21_out, and_144_out);
  and and_109 (and_109_out, and_144_out, ALA_out);
  and and_110 (and_110_out, and_144_out, ALI_out);
  and and_111 (and_111_out, and_144_out, LDI_out);
  and and_112 (and_112_out, and_144_out, PSH_out);
  or or_22 (or_22_out, not_6_out, JMP_out);
  and and_113 (and_113_out, and_144_out, JSR_out);
  and and_114 (and_114_out, and_144_out, RSR_out);
  and and_115 (and_115_out, and_144_out, HLT_out);
  nor nor_180 (nor_180_out, nor_177_out, and_157_out);
  nor nor_181 (nor_181_out, nor_180_out, and_157_out);
  nor nor_182 (nor_182_out, nor_178_out, and_157_out);
  nor nor_183 (nor_183_out, nor_182_out, and_157_out);
  nor nor_184 (nor_184_out, nor_179_out, and_157_out);
  nor nor_185 (nor_185_out, nor_184_out, and_157_out);
  and and_116 (and_116_out, or_20_out, and_144_out);
  and and_117 (and_117_out, or_20_out, and_145_out);
  and and_118 (and_118_out, and_144_out, ALS_out);
  and and_119 (and_119_out, and_145_out, ALS_out);
  and and_120 (and_120_out, and_144_out, POP_out);
  and and_121 (and_121_out, and_145_out, POP_out);
  and and_122 (and_122_out, or_22_out, and_144_out);
  and and_123 (and_123_out, or_22_out, and_145_out);
  and and_124 (and_124_out, and_145_out, JSR_out);
  and and_125 (and_125_out, and_145_out, RSR_out);
  not not_7 (not_7_out, nor_241_out);
  nor nor_186 (nor_186_out, nor_180_out, or_24_out, nor_187_out);
  nor nor_187 (nor_187_out, nor_186_out, nor_181_out);
  nor nor_188 (nor_188_out, nor_182_out, or_24_out, nor_189_out);
  nor nor_189 (nor_189_out, nor_188_out, nor_183_out);
  nor nor_190 (nor_190_out, nor_184_out, or_24_out, nor_191_out);
  nor nor_191 (nor_191_out, nor_190_out, nor_185_out);
  and and_126 (and_126_out, and_146_out, ALM_out);
  and and_127 (and_127_out, and_146_out, LOD_out);
  and and_128 (and_128_out, and_146_out, STO_out);
  and and_129 (and_129_out, or_22_out, and_146_out);
  and and_130 (and_130_out, and_146_out, JSR_out);
  and and_131 (and_131_out, and_146_out, RSR_out);
  and and_132 (and_132_out, nor_186_out, and_157_out);
  and and_133 (and_133_out, and_157_out, nor_187_out);
  and and_134 (and_134_out, nor_188_out, and_157_out);
  and and_135 (and_135_out, and_157_out, nor_189_out);
  and and_136 (and_136_out, nor_190_out, and_157_out);
  and and_137 (and_137_out, and_157_out, nor_191_out);
  and and_138 (and_138_out, and_147_out, JSR_out);
  and and_139 (and_139_out, and_147_out, RSR_out);
  nor nor_192 (nor_192_out, and_132_out, nor_193_out);
  nor nor_193 (nor_193_out, nor_192_out, or_24_out, and_133_out);
  nor nor_194 (nor_194_out, and_134_out, nor_195_out);
  nor nor_195 (nor_195_out, nor_194_out, or_24_out, and_135_out);
  and and_140 (and_140_out, nor_193_out, nor_195_out);
  nor nor_196 (nor_196_out, and_136_out, nor_197_out);
  nor nor_197 (nor_197_out, nor_196_out, or_24_out, and_137_out);
  and and_141 (and_141_out, and_148_out, JSR_out);
  and and_142 (and_142_out, and_148_out, RSR_out);
  xnor xnor_9 (xnor_9_out, nor_193_out, nor_195_out);
  xnor xnor_10 (xnor_10_out, and_140_out, nor_197_out);
  and and_143 (and_143_out, nor_192_out, nor_194_out, nor_196_out);
  and and_144 (and_144_out, nor_193_out, nor_194_out, nor_196_out);
  and and_145 (and_145_out, nor_192_out, nor_195_out, nor_196_out);
  and and_146 (and_146_out, nor_193_out, nor_195_out, nor_196_out);
  and and_147 (and_147_out, nor_192_out, nor_194_out, nor_197_out);
  and and_148 (and_148_out, nor_193_out, nor_194_out, nor_197_out);
  or or_23 (or_23_out, nor_240_out, and_143_out);
  buf IRI (IRI_out, or_23_out);
  buf A2I (A2I_out, and_117_out);
  buf P1O (P1O_out, and_113_out);
  buf P2O (P2O_out, and_124_out);
  or RST (RST_out, and_108_out, and_126_out, and_109_out, and_110_out, and_119_out, and_127_out, and_111_out, and_128_out, and_112_out, and_121_out, and_129_out, and_141_out, and_142_out);
  or LOD_2 (LOD_2_out, and_127_out, and_111_out, and_121_out);
  or FRI (FRI_out, and_126_out, and_109_out, and_110_out, and_119_out);
  or ARI (ARI_out, and_126_out, and_109_out, and_110_out, and_119_out, and_127_out, and_111_out, and_121_out);
  or ARO (ARO_out, and_109_out, and_128_out, and_112_out);
  or A1I (A1I_out, and_116_out, and_122_out, and_130_out);
  or A1O (A1O_out, and_129_out, and_141_out);
  or P1I (P1I_out, and_129_out, and_141_out, and_131_out);
  or P2I (P2I_out, and_123_out, and_138_out, and_125_out);
  or PCI (PCI_out, or_23_out, and_116_out, and_117_out, and_110_out, and_111_out, and_122_out, and_130_out, and_139_out, and_142_out);
  or STI (STI_out, and_118_out, and_112_out, and_120_out, and_113_out, and_124_out, and_114_out, and_125_out);
  or STD (STD_out, and_118_out, and_120_out, and_114_out, and_125_out);
  or ADR (ADR_out, and_126_out, and_127_out, and_128_out);
  or PRC (PRC_out, or_23_out, and_116_out, and_117_out, and_110_out, and_111_out, and_122_out, and_123_out, and_130_out, and_138_out);
  or STP (STP_out, and_119_out, and_112_out, and_121_out, and_113_out, and_124_out, and_125_out, and_131_out);
  nor RD (RD_out, and_108_out, and_109_out, and_118_out, and_128_out, and_120_out, not_7_out, and_129_out, and_113_out, and_124_out, and_141_out, and_114_out);
  or WR (WR_out, and_128_out, and_112_out, not_7_out, and_113_out, and_124_out);
  nor nor_198 (nor_198_out, nor_242_out, A1I_out);
  and and_149 (and_149_out, A1I_out, in_1);
  nor nor_199 (nor_199_out, nor_244_out, A1I_out);
  and and_150 (and_150_out, A1I_out, in_2);
  nor nor_200 (nor_200_out, nor_246_out, A1I_out);
  and and_151 (and_151_out, A1I_out, in_3);
  nor nor_201 (nor_201_out, nor_248_out, A1I_out);
  and and_152 (and_152_out, A1I_out, in_4);
  nor nor_202 (nor_202_out, nor_250_out, A1I_out);
  and and_153 (and_153_out, A1I_out, in_5);
  nor nor_203 (nor_203_out, nor_252_out, A1I_out);
  and and_154 (and_154_out, A1I_out, in_6);
  nor nor_204 (nor_204_out, nor_254_out, A1I_out);
  and and_155 (and_155_out, A1I_out, in_8);
  nor nor_205 (nor_205_out, nor_256_out, A1I_out);
  and and_156 (and_156_out, A1I_out, in_9);
  Clock clock_1 (.out(clock_1_out));
  nor nor_206 (nor_206_out, and_115_out, nor_207_out);
  nor nor_207 (nor_207_out, nor_206_out, or_24_out);
  nor nor_208 (nor_208_out, nor_198_out, and_149_out, and_157_out);
  nor nor_209 (nor_209_out, nor_208_out, and_157_out);
  nor nor_210 (nor_210_out, nor_199_out, and_150_out, and_157_out);
  nor nor_211 (nor_211_out, nor_210_out, and_157_out);
  nor nor_212 (nor_212_out, nor_200_out, and_151_out, and_157_out);
  nor nor_213 (nor_213_out, nor_212_out, and_157_out);
  nor nor_214 (nor_214_out, nor_201_out, and_152_out, and_157_out);
  nor nor_215 (nor_215_out, nor_214_out, and_157_out);
  nor nor_216 (nor_216_out, nor_202_out, and_153_out, and_157_out);
  nor nor_217 (nor_217_out, nor_216_out, and_157_out);
  nor nor_218 (nor_218_out, nor_203_out, and_154_out, and_157_out);
  nor nor_219 (nor_219_out, nor_218_out, and_157_out);
  nor nor_220 (nor_220_out, nor_204_out, and_155_out, and_157_out);
  nor nor_221 (nor_221_out, nor_220_out, and_157_out);
  nor nor_222 (nor_222_out, nor_205_out, and_156_out, and_157_out);
  nor nor_223 (nor_223_out, nor_222_out, and_157_out);
  and and_157 (and_157_out, clock_1_out, nor_206_out);
  nor nor_224 (nor_224_out, nor_208_out, nor_225_out);
  nor nor_225 (nor_225_out, nor_224_out, nor_209_out);
  nor nor_226 (nor_226_out, nor_210_out, nor_227_out);
  nor nor_227 (nor_227_out, nor_226_out, nor_211_out);
  nor nor_228 (nor_228_out, nor_212_out, nor_229_out);
  nor nor_229 (nor_229_out, nor_228_out, nor_213_out);
  nor nor_230 (nor_230_out, nor_214_out, nor_231_out);
  nor nor_231 (nor_231_out, nor_230_out, nor_215_out);
  nor nor_232 (nor_232_out, nor_216_out, nor_233_out);
  nor nor_233 (nor_233_out, nor_232_out, nor_217_out);
  nor nor_234 (nor_234_out, nor_218_out, nor_235_out);
  nor nor_235 (nor_235_out, nor_234_out, nor_219_out);
  nor nor_236 (nor_236_out, nor_220_out, nor_237_out);
  nor nor_237 (nor_237_out, nor_236_out, nor_221_out);
  nor nor_238 (nor_238_out, nor_222_out, nor_239_out);
  nor nor_239 (nor_239_out, nor_238_out, nor_223_out);
  or or_24 (or_24_out, HRD_RST_out, SFT_RST_out);
  and and_158 (and_158_out, nor_224_out, and_157_out);
  and and_159 (and_159_out, and_157_out, nor_225_out);
  and and_160 (and_160_out, nor_226_out, and_157_out);
  and and_161 (and_161_out, and_157_out, nor_227_out);
  and and_162 (and_162_out, nor_228_out, and_157_out);
  and and_163 (and_163_out, and_157_out, nor_229_out);
  and and_164 (and_164_out, nor_230_out, and_157_out);
  and and_165 (and_165_out, and_157_out, nor_231_out);
  and and_166 (and_166_out, nor_232_out, and_157_out);
  and and_167 (and_167_out, and_157_out, nor_233_out);
  and and_168 (and_168_out, nor_234_out, and_157_out);
  and and_169 (and_169_out, and_157_out, nor_235_out);
  and and_170 (and_170_out, nor_236_out, and_157_out);
  and and_171 (and_171_out, and_157_out, nor_237_out);
  and and_172 (and_172_out, nor_238_out, and_157_out);
  and and_173 (and_173_out, and_157_out, nor_239_out);
  nor nor_240 (nor_240_out, and_261_out, SFT_RST_out, nor_241_out);
  nor nor_241 (nor_241_out, nor_240_out, HRD_RST_out);
  nor nor_242 (nor_242_out, and_158_out, nor_243_out);
  nor nor_243 (nor_243_out, nor_242_out, and_159_out);
  nor nor_244 (nor_244_out, and_160_out, nor_245_out);
  nor nor_245 (nor_245_out, nor_244_out, and_161_out);
  nor nor_246 (nor_246_out, and_162_out, nor_247_out);
  nor nor_247 (nor_247_out, nor_246_out, and_163_out);
  nor nor_248 (nor_248_out, and_164_out, nor_249_out);
  nor nor_249 (nor_249_out, nor_248_out, and_165_out);
  nor nor_250 (nor_250_out, and_166_out, nor_251_out);
  nor nor_251 (nor_251_out, nor_250_out, and_167_out);
  nor nor_252 (nor_252_out, and_168_out, nor_253_out);
  nor nor_253 (nor_253_out, nor_252_out, and_169_out);
  nor nor_254 (nor_254_out, and_170_out, nor_255_out);
  nor nor_255 (nor_255_out, nor_254_out, and_171_out);
  nor nor_256 (nor_256_out, and_172_out, nor_257_out);
  nor nor_257 (nor_257_out, nor_256_out, and_173_out);
  nand OC_9 (OC_9_out[0], nor_242_out, ADR_out);
  nand OC_10 (in_1, nor_242_out, A1O_out);
  nand OC_11 (OC_9_out[1], nor_244_out, ADR_out);
  nand OC_12 (in_2, nor_244_out, A1O_out);
  nand OC_13 (OC_9_out[2], nor_246_out, ADR_out);
  nand OC_14 (in_3, nor_246_out, A1O_out);
  nand OC_15 (OC_9_out[3], nor_248_out, ADR_out);
  nand OC_16 (in_4, nor_248_out, A1O_out);
  nand OC_17 (OC_9_out[4], nor_250_out, ADR_out);
  nand OC_18 (in_5, nor_250_out, A1O_out);
  nand OC_19 (OC_9_out[5], nor_252_out, ADR_out);
  nand OC_20 (in_6, nor_252_out, A1O_out);
  nand OC_21 (OC_9_out[6], nor_254_out, ADR_out);
  nand OC_22 (in_8, nor_254_out, A1O_out);
  nand OC_23 (OC_9_out[7], nor_256_out, ADR_out);
  nand OC_24 (in_9, nor_256_out, A1O_out);
  Pull_Resistor #(.pull(1)) pull_resistor_9 (.node(OC_9_out[0]));
  Pull_Resistor #(.pull(1)) pull_resistor_10 (.node(OC_9_out[1]));
  Pull_Resistor #(.pull(1)) pull_resistor_11 (.node(OC_9_out[2]));
  Pull_Resistor #(.pull(1)) pull_resistor_12 (.node(OC_9_out[3]));
  Pull_Resistor #(.pull(1)) pull_resistor_13 (.node(OC_9_out[4]));
  Pull_Resistor #(.pull(1)) pull_resistor_14 (.node(OC_9_out[5]));
  Pull_Resistor #(.pull(1)) pull_resistor_15 (.node(OC_9_out[6]));
  Pull_Resistor #(.pull(1)) pull_resistor_16 (.node(OC_9_out[7]));
  nor nor_258 (nor_258_out, nor_298_out, A2I_out);
  and and_174 (and_174_out, A2I_out, in_1);
  nor nor_259 (nor_259_out, nor_300_out, A2I_out);
  and and_175 (and_175_out, A2I_out, in_2);
  nor nor_260 (nor_260_out, nor_302_out, A2I_out);
  and and_176 (and_176_out, A2I_out, in_3);
  nor nor_261 (nor_261_out, nor_304_out, A2I_out);
  and and_177 (and_177_out, A2I_out, in_4);
  nor nor_262 (nor_262_out, nor_306_out, A2I_out);
  and and_178 (and_178_out, A2I_out, in_5);
  nor nor_263 (nor_263_out, nor_308_out, A2I_out);
  and and_179 (and_179_out, A2I_out, in_6);
  nor nor_264 (nor_264_out, nor_310_out, A2I_out);
  and and_180 (and_180_out, A2I_out, in_8);
  nor nor_265 (nor_265_out, nor_312_out, A2I_out);
  and and_181 (and_181_out, A2I_out, in_9);
  nor nor_266 (nor_266_out, nor_258_out, and_174_out, and_157_out);
  nor nor_267 (nor_267_out, nor_266_out, and_157_out);
  nor nor_268 (nor_268_out, nor_259_out, and_175_out, and_157_out);
  nor nor_269 (nor_269_out, nor_268_out, and_157_out);
  nor nor_270 (nor_270_out, nor_260_out, and_176_out, and_157_out);
  nor nor_271 (nor_271_out, nor_270_out, and_157_out);
  nor nor_272 (nor_272_out, nor_261_out, and_177_out, and_157_out);
  nor nor_273 (nor_273_out, nor_272_out, and_157_out);
  nor nor_274 (nor_274_out, nor_262_out, and_178_out, and_157_out);
  nor nor_275 (nor_275_out, nor_274_out, and_157_out);
  nor nor_276 (nor_276_out, nor_263_out, and_179_out, and_157_out);
  nor nor_277 (nor_277_out, nor_276_out, and_157_out);
  nor nor_278 (nor_278_out, nor_264_out, and_180_out, and_157_out);
  nor nor_279 (nor_279_out, nor_278_out, and_157_out);
  nor nor_280 (nor_280_out, nor_265_out, and_181_out, and_157_out);
  nor nor_281 (nor_281_out, nor_280_out, and_157_out);
  and and_182 (and_182_out, nor_282_out, and_157_out);
  nor nor_282 (nor_282_out, nor_266_out, nor_283_out);
  and and_183 (and_183_out, and_157_out, nor_283_out);
  nor nor_283 (nor_283_out, nor_282_out, nor_267_out);
  and and_184 (and_184_out, nor_284_out, and_157_out);
  nor nor_284 (nor_284_out, nor_268_out, nor_285_out);
  and and_185 (and_185_out, and_157_out, nor_285_out);
  nor nor_285 (nor_285_out, nor_284_out, nor_269_out);
  nor nor_286 (nor_286_out, nor_270_out, nor_287_out);
  and and_186 (and_186_out, nor_286_out, and_157_out);
  nor nor_287 (nor_287_out, nor_286_out, nor_271_out);
  and and_187 (and_187_out, and_157_out, nor_287_out);
  and and_188 (and_188_out, nor_288_out, and_157_out);
  nor nor_288 (nor_288_out, nor_272_out, nor_289_out);
  nor nor_289 (nor_289_out, nor_288_out, nor_273_out);
  and and_189 (and_189_out, and_157_out, nor_289_out);
  nor nor_290 (nor_290_out, nor_274_out, nor_291_out);
  and and_190 (and_190_out, nor_290_out, and_157_out);
  nor nor_291 (nor_291_out, nor_290_out, nor_275_out);
  and and_191 (and_191_out, and_157_out, nor_291_out);
  nor nor_292 (nor_292_out, nor_276_out, nor_293_out);
  and and_192 (and_192_out, nor_292_out, and_157_out);
  nor nor_293 (nor_293_out, nor_292_out, nor_277_out);
  and and_193 (and_193_out, and_157_out, nor_293_out);
  nor nor_294 (nor_294_out, nor_278_out, nor_295_out);
  and and_194 (and_194_out, nor_294_out, and_157_out);
  and and_195 (and_195_out, and_157_out, nor_295_out);
  nor nor_295 (nor_295_out, nor_294_out, nor_279_out);
  and and_196 (and_196_out, nor_296_out, and_157_out);
  nor nor_296 (nor_296_out, nor_280_out, nor_297_out);
  and and_197 (and_197_out, and_157_out, nor_297_out);
  nor nor_297 (nor_297_out, nor_296_out, nor_281_out);
  nor nor_298 (nor_298_out, and_182_out, nor_299_out);
  nor nor_299 (nor_299_out, nor_298_out, and_183_out);
  nor nor_300 (nor_300_out, and_184_out, nor_301_out);
  nor nor_301 (nor_301_out, nor_300_out, and_185_out);
  nor nor_302 (nor_302_out, and_186_out, nor_303_out);
  nor nor_303 (nor_303_out, nor_302_out, and_187_out);
  nor nor_304 (nor_304_out, and_188_out, nor_305_out);
  nor nor_305 (nor_305_out, nor_304_out, and_189_out);
  nor nor_306 (nor_306_out, and_190_out, nor_307_out);
  nor nor_307 (nor_307_out, nor_306_out, and_191_out);
  nor nor_308 (nor_308_out, and_192_out, nor_309_out);
  nor nor_309 (nor_309_out, nor_308_out, and_193_out);
  nor nor_310 (nor_310_out, and_194_out, nor_311_out);
  nor nor_311 (nor_311_out, nor_310_out, and_195_out);
  nor nor_312 (nor_312_out, and_196_out, nor_313_out);
  nor nor_313 (nor_313_out, nor_312_out, and_197_out);
  nand OC_25 (OC_9_out[8], nor_298_out, ADR_out);
  nand OC_26 (OC_9_out[9], nor_300_out, ADR_out);
  nand OC_27 (OC_9_out[10], nor_302_out, ADR_out);
  nand OC_28 (OC_9_out[11], nor_304_out, ADR_out);
  nand OC_29 (OC_9_out[12], nor_306_out, ADR_out);
  nand OC_30 (OC_9_out[13], nor_308_out, ADR_out);
  nand OC_31 (OC_9_out[14], nor_310_out, ADR_out);
  nand OC_32 (OC_9_out[15], nor_312_out, ADR_out);
  Pull_Resistor #(.pull(1)) pull_resistor_17 (.node(OC_9_out[8]));
  Pull_Resistor #(.pull(1)) pull_resistor_18 (.node(OC_9_out[9]));
  Pull_Resistor #(.pull(1)) pull_resistor_19 (.node(OC_9_out[10]));
  Pull_Resistor #(.pull(1)) pull_resistor_20 (.node(OC_9_out[11]));
  Pull_Resistor #(.pull(1)) pull_resistor_21 (.node(OC_9_out[12]));
  Pull_Resistor #(.pull(1)) pull_resistor_22 (.node(OC_9_out[13]));
  Pull_Resistor #(.pull(1)) pull_resistor_23 (.node(OC_9_out[14]));
  Pull_Resistor #(.pull(1)) pull_resistor_24 (.node(OC_9_out[15]));
  nor nor_314 (nor_314_out, xnor_11_out, P1I_out);
  and and_198 (and_198_out, P1I_out, in_1);
  nor nor_315 (nor_315_out, xnor_12_out, P1I_out);
  and and_199 (and_199_out, P1I_out, in_2);
  nor nor_316 (nor_316_out, xnor_13_out, P1I_out);
  and and_200 (and_200_out, P1I_out, in_3);
  nor nor_317 (nor_317_out, xnor_14_out, P1I_out);
  and and_201 (and_201_out, P1I_out, in_4);
  nor nor_318 (nor_318_out, xnor_15_out, P1I_out);
  and and_202 (and_202_out, P1I_out, in_5);
  nor nor_319 (nor_319_out, xnor_16_out, P1I_out);
  and and_203 (and_203_out, P1I_out, in_6);
  nor nor_320 (nor_320_out, xnor_17_out, P1I_out);
  and and_204 (and_204_out, P1I_out, in_8);
  nor nor_321 (nor_321_out, xnor_18_out, P1I_out);
  and and_205 (and_205_out, P1I_out, in_9);
  nor nor_322 (nor_322_out, nor_314_out, and_198_out, and_157_out);
  nor nor_323 (nor_323_out, nor_322_out, and_157_out);
  nor nor_324 (nor_324_out, nor_315_out, and_199_out, and_157_out);
  nor nor_325 (nor_325_out, nor_324_out, and_157_out);
  nor nor_326 (nor_326_out, nor_316_out, and_200_out, and_157_out);
  nor nor_327 (nor_327_out, nor_326_out, and_157_out);
  nor nor_328 (nor_328_out, nor_317_out, and_201_out, and_157_out);
  nor nor_329 (nor_329_out, nor_328_out, and_157_out);
  nor nor_330 (nor_330_out, nor_318_out, and_202_out, and_157_out);
  nor nor_331 (nor_331_out, nor_330_out, and_157_out);
  nor nor_332 (nor_332_out, nor_319_out, and_203_out, and_157_out);
  nor nor_333 (nor_333_out, nor_332_out, and_157_out);
  nor nor_334 (nor_334_out, nor_320_out, and_204_out, and_157_out);
  nor nor_335 (nor_335_out, nor_334_out, and_157_out);
  nor nor_336 (nor_336_out, nor_321_out, and_205_out, and_157_out);
  nor nor_337 (nor_337_out, nor_336_out, and_157_out);
  nor nor_338 (nor_338_out, nor_322_out, or_24_out, nor_339_out);
  and and_206 (and_206_out, nor_338_out, and_157_out);
  and and_207 (and_207_out, and_157_out, nor_339_out);
  nor nor_339 (nor_339_out, nor_338_out, nor_323_out);
  and and_208 (and_208_out, nor_340_out, and_157_out);
  nor nor_340 (nor_340_out, nor_324_out, or_24_out, nor_341_out);
  nor nor_341 (nor_341_out, nor_340_out, nor_325_out);
  and and_209 (and_209_out, and_157_out, nor_341_out);
  nor nor_342 (nor_342_out, nor_326_out, or_24_out, nor_343_out);
  and and_210 (and_210_out, nor_342_out, and_157_out);
  and and_211 (and_211_out, and_157_out, nor_343_out);
  nor nor_343 (nor_343_out, nor_342_out, nor_327_out);
  and and_212 (and_212_out, nor_344_out, and_157_out);
  nor nor_344 (nor_344_out, nor_328_out, or_24_out, nor_345_out);
  nor nor_345 (nor_345_out, nor_344_out, nor_329_out);
  and and_213 (and_213_out, and_157_out, nor_345_out);
  nor nor_346 (nor_346_out, nor_330_out, or_24_out, nor_347_out);
  and and_214 (and_214_out, nor_346_out, and_157_out);
  and and_215 (and_215_out, and_157_out, nor_347_out);
  nor nor_347 (nor_347_out, nor_346_out, nor_331_out);
  and and_216 (and_216_out, nor_348_out, and_157_out);
  nor nor_348 (nor_348_out, nor_332_out, or_24_out, nor_349_out);
  and and_217 (and_217_out, and_157_out, nor_349_out);
  nor nor_349 (nor_349_out, nor_348_out, nor_333_out);
  and and_218 (and_218_out, nor_350_out, and_157_out);
  nor nor_350 (nor_350_out, nor_334_out, or_24_out, nor_351_out);
  nor nor_351 (nor_351_out, nor_350_out, nor_335_out);
  and and_219 (and_219_out, and_157_out, nor_351_out);
  nor nor_352 (nor_352_out, nor_336_out, or_24_out, nor_353_out);
  and and_220 (and_220_out, nor_352_out, and_157_out);
  nor nor_353 (nor_353_out, nor_352_out, nor_337_out);
  and and_221 (and_221_out, and_157_out, nor_353_out);
  nor nor_354 (nor_354_out, and_206_out, nor_355_out);
  nor nor_355 (nor_355_out, nor_354_out, or_24_out, and_207_out);
  nor nor_356 (nor_356_out, and_208_out, nor_357_out);
  nor nor_357 (nor_357_out, nor_356_out, or_24_out, and_209_out);
  nor nor_358 (nor_358_out, and_210_out, nor_359_out);
  nor nor_359 (nor_359_out, nor_358_out, or_24_out, and_211_out);
  nor nor_360 (nor_360_out, and_212_out, nor_361_out);
  nor nor_361 (nor_361_out, nor_360_out, or_24_out, and_213_out);
  nor nor_362 (nor_362_out, and_214_out, nor_363_out);
  nor nor_363 (nor_363_out, nor_362_out, or_24_out, and_215_out);
  nor nor_364 (nor_364_out, and_216_out, nor_365_out);
  nor nor_365 (nor_365_out, nor_364_out, or_24_out, and_217_out);
  nor nor_366 (nor_366_out, and_218_out, nor_367_out);
  nor nor_367 (nor_367_out, nor_366_out, or_24_out, and_219_out);
  nor nor_368 (nor_368_out, and_220_out, nor_369_out);
  nor nor_369 (nor_369_out, nor_368_out, or_24_out, and_221_out);
  xnor xnor_11 (xnor_11_out, PCI_out, nor_355_out);
  and and_222 (and_222_out, PCI_out, nor_355_out);
  xnor xnor_12 (xnor_12_out, and_222_out, nor_357_out);
  and and_223 (and_223_out, and_222_out, nor_357_out);
  xnor xnor_13 (xnor_13_out, and_223_out, nor_359_out);
  and and_224 (and_224_out, and_223_out, nor_359_out);
  xnor xnor_14 (xnor_14_out, and_224_out, nor_361_out);
  and and_225 (and_225_out, and_224_out, nor_361_out);
  xnor xnor_15 (xnor_15_out, and_225_out, nor_363_out);
  and and_226 (and_226_out, and_225_out, nor_363_out);
  xnor xnor_16 (xnor_16_out, and_226_out, nor_365_out);
  and and_227 (and_227_out, and_226_out, nor_365_out);
  xnor xnor_17 (xnor_17_out, and_227_out, nor_367_out);
  and and_228 (and_228_out, and_227_out, nor_367_out);
  xnor xnor_18 (xnor_18_out, and_228_out, nor_369_out);
  and and_229 (and_229_out, and_228_out, nor_369_out);
  nand OC_33 (in_1, P1O_out, nor_354_out);
  nand OC_34 (OC_9_out[0], nor_354_out, PRC_out);
  nand OC_35 (in_2, P1O_out, nor_356_out);
  nand OC_36 (OC_9_out[1], nor_356_out, PRC_out);
  nand OC_37 (in_3, P1O_out, nor_358_out);
  nand OC_38 (OC_9_out[2], nor_358_out, PRC_out);
  nand OC_39 (in_4, P1O_out, nor_360_out);
  nand OC_40 (OC_9_out[3], nor_360_out, PRC_out);
  nand OC_41 (in_5, P1O_out, nor_362_out);
  nand OC_42 (OC_9_out[4], nor_362_out, PRC_out);
  nand OC_43 (in_6, P1O_out, nor_364_out);
  nand OC_44 (OC_9_out[5], nor_364_out, PRC_out);
  nand OC_45 (in_8, P1O_out, nor_366_out);
  nand OC_46 (OC_9_out[6], nor_366_out, PRC_out);
  nand OC_47 (in_9, P1O_out, nor_368_out);
  nand OC_48 (OC_9_out[7], nor_368_out, PRC_out);
  nor nor_370 (nor_370_out, xnor_19_out, P2I_out);
  and and_230 (and_230_out, P2I_out, in_1);
  nor nor_371 (nor_371_out, xnor_20_out, P2I_out);
  and and_231 (and_231_out, P2I_out, in_2);
  nor nor_372 (nor_372_out, xnor_21_out, P2I_out);
  and and_232 (and_232_out, P2I_out, in_3);
  nor nor_373 (nor_373_out, xnor_22_out, P2I_out);
  and and_233 (and_233_out, P2I_out, in_4);
  nor nor_374 (nor_374_out, xnor_23_out, P2I_out);
  and and_234 (and_234_out, P2I_out, in_5);
  nor nor_375 (nor_375_out, xnor_24_out, P2I_out);
  and and_235 (and_235_out, P2I_out, in_6);
  nor nor_376 (nor_376_out, xnor_25_out, P2I_out);
  and and_236 (and_236_out, P2I_out, in_8);
  nor nor_377 (nor_377_out, xnor_26_out, P2I_out);
  and and_237 (and_237_out, P2I_out, in_9);
  nor nor_378 (nor_378_out, nor_370_out, and_230_out, and_157_out);
  nor nor_379 (nor_379_out, nor_378_out, and_157_out);
  nor nor_380 (nor_380_out, nor_371_out, and_231_out, and_157_out);
  nor nor_381 (nor_381_out, nor_380_out, and_157_out);
  nor nor_382 (nor_382_out, nor_372_out, and_232_out, and_157_out);
  nor nor_383 (nor_383_out, nor_382_out, and_157_out);
  nor nor_384 (nor_384_out, nor_373_out, and_233_out, and_157_out);
  nor nor_385 (nor_385_out, nor_384_out, and_157_out);
  nor nor_386 (nor_386_out, nor_374_out, and_234_out, and_157_out);
  nor nor_387 (nor_387_out, nor_386_out, and_157_out);
  nor nor_388 (nor_388_out, nor_375_out, and_235_out, and_157_out);
  nor nor_389 (nor_389_out, nor_388_out, and_157_out);
  nor nor_390 (nor_390_out, nor_376_out, and_236_out, and_157_out);
  nor nor_391 (nor_391_out, nor_390_out, and_157_out);
  nor nor_392 (nor_392_out, nor_377_out, and_237_out, and_157_out);
  nor nor_393 (nor_393_out, nor_392_out, and_157_out);
  nor nor_394 (nor_394_out, nor_378_out, or_24_out, nor_395_out);
  nor nor_395 (nor_395_out, nor_394_out, nor_379_out);
  nor nor_396 (nor_396_out, nor_380_out, or_24_out, nor_397_out);
  nor nor_397 (nor_397_out, nor_396_out, nor_381_out);
  nor nor_398 (nor_398_out, nor_382_out, or_24_out, nor_399_out);
  nor nor_399 (nor_399_out, nor_398_out, nor_383_out);
  nor nor_400 (nor_400_out, nor_384_out, or_24_out, nor_401_out);
  nor nor_401 (nor_401_out, nor_400_out, nor_385_out);
  nor nor_402 (nor_402_out, nor_386_out, or_24_out, nor_403_out);
  nor nor_403 (nor_403_out, nor_402_out, nor_387_out);
  nor nor_404 (nor_404_out, nor_388_out, or_24_out, nor_405_out);
  nor nor_405 (nor_405_out, nor_404_out, nor_389_out);
  nor nor_406 (nor_406_out, nor_390_out, or_24_out, nor_407_out);
  nor nor_407 (nor_407_out, nor_406_out, nor_391_out);
  nor nor_408 (nor_408_out, nor_392_out, or_24_out, nor_409_out);
  nor nor_409 (nor_409_out, nor_408_out, nor_393_out);
  and and_238 (and_238_out, nor_394_out, and_157_out);
  and and_239 (and_239_out, and_157_out, nor_395_out);
  and and_240 (and_240_out, nor_396_out, and_157_out);
  and and_241 (and_241_out, and_157_out, nor_397_out);
  and and_242 (and_242_out, nor_398_out, and_157_out);
  and and_243 (and_243_out, and_157_out, nor_399_out);
  and and_244 (and_244_out, nor_400_out, and_157_out);
  and and_245 (and_245_out, and_157_out, nor_401_out);
  and and_246 (and_246_out, nor_402_out, and_157_out);
  and and_247 (and_247_out, and_157_out, nor_403_out);
  and and_248 (and_248_out, nor_404_out, and_157_out);
  and and_249 (and_249_out, and_157_out, nor_405_out);
  and and_250 (and_250_out, nor_406_out, and_157_out);
  and and_251 (and_251_out, and_157_out, nor_407_out);
  and and_252 (and_252_out, nor_408_out, and_157_out);
  and and_253 (and_253_out, and_157_out, nor_409_out);
  nor nor_410 (nor_410_out, and_238_out, nor_411_out);
  nor nor_411 (nor_411_out, nor_410_out, or_24_out, and_239_out);
  nor nor_412 (nor_412_out, and_240_out, nor_413_out);
  nor nor_413 (nor_413_out, nor_412_out, or_24_out, and_241_out);
  nor nor_414 (nor_414_out, and_242_out, nor_415_out);
  nor nor_415 (nor_415_out, nor_414_out, or_24_out, and_243_out);
  nor nor_416 (nor_416_out, and_244_out, nor_417_out);
  nor nor_417 (nor_417_out, nor_416_out, or_24_out, and_245_out);
  nor nor_418 (nor_418_out, and_246_out, nor_419_out);
  nor nor_419 (nor_419_out, nor_418_out, or_24_out, and_247_out);
  nor nor_420 (nor_420_out, and_248_out, nor_421_out);
  nor nor_421 (nor_421_out, nor_420_out, or_24_out, and_249_out);
  nor nor_422 (nor_422_out, and_250_out, nor_423_out);
  nor nor_423 (nor_423_out, nor_422_out, or_24_out, and_251_out);
  nor nor_424 (nor_424_out, and_252_out, nor_425_out);
  nor nor_425 (nor_425_out, nor_424_out, or_24_out, and_253_out);
  xnor xnor_19 (xnor_19_out, and_229_out, nor_411_out);
  and and_254 (and_254_out, and_229_out, nor_411_out);
  xnor xnor_20 (xnor_20_out, and_254_out, nor_413_out);
  and and_255 (and_255_out, and_254_out, nor_413_out);
  xnor xnor_21 (xnor_21_out, and_255_out, nor_415_out);
  and and_256 (and_256_out, and_255_out, nor_415_out);
  xnor xnor_22 (xnor_22_out, and_256_out, nor_417_out);
  and and_257 (and_257_out, and_256_out, nor_417_out);
  xnor xnor_23 (xnor_23_out, and_257_out, nor_419_out);
  and and_258 (and_258_out, and_257_out, nor_419_out);
  xnor xnor_24 (xnor_24_out, and_258_out, nor_421_out);
  and and_259 (and_259_out, and_258_out, nor_421_out);
  xnor xnor_25 (xnor_25_out, and_259_out, nor_423_out);
  and and_260 (and_260_out, and_259_out, nor_423_out);
  xnor xnor_26 (xnor_26_out, and_260_out, nor_425_out);
  and and_261 (and_261_out, and_260_out, nor_425_out);
  nand OC_49 (in_1, P2O_out, nor_410_out);
  nand OC_50 (OC_9_out[8], nor_410_out, PRC_out);
  nand OC_51 (in_2, P2O_out, nor_412_out);
  nand OC_52 (OC_9_out[9], nor_412_out, PRC_out);
  nand OC_53 (in_3, P2O_out, nor_414_out);
  nand OC_54 (OC_9_out[10], nor_414_out, PRC_out);
  nand OC_55 (in_4, P2O_out, xnor_22_out);
  nand OC_56 (OC_9_out[11], xnor_22_out, PRC_out);
  nand OC_57 (in_5, P2O_out, nor_418_out);
  nand OC_58 (OC_9_out[12], nor_418_out, PRC_out);
  nand OC_59 (in_6, P2O_out, nor_420_out);
  nand OC_60 (OC_9_out[13], nor_420_out, PRC_out);
  nand OC_61 (in_8, P2O_out, nor_422_out);
  nand OC_62 (OC_9_out[14], nor_422_out, PRC_out);
  nand OC_63 (in_9, P2O_out, nor_424_out);
  nand OC_64 (OC_9_out[15], nor_424_out, PRC_out);
  nor nor_426 (nor_426_out, xnor_34_out, and_157_out);
  nor nor_427 (nor_427_out, nor_426_out, and_157_out);
  nor nor_428 (nor_428_out, xnor_35_out, and_157_out);
  nor nor_429 (nor_429_out, nor_428_out, and_157_out);
  nor nor_430 (nor_430_out, xnor_36_out, and_157_out);
  nor nor_431 (nor_431_out, nor_430_out, and_157_out);
  nor nor_432 (nor_432_out, xnor_37_out, and_157_out);
  nor nor_433 (nor_433_out, nor_432_out, and_157_out);
  nor nor_434 (nor_434_out, xnor_38_out, and_157_out);
  nor nor_435 (nor_435_out, nor_434_out, and_157_out);
  nor nor_436 (nor_436_out, xnor_39_out, and_157_out);
  nor nor_437 (nor_437_out, nor_436_out, and_157_out);
  nor nor_438 (nor_438_out, xnor_40_out, and_157_out);
  nor nor_439 (nor_439_out, nor_438_out, and_157_out);
  nor nor_440 (nor_440_out, xnor_41_out, and_157_out);
  nor nor_441 (nor_441_out, nor_440_out, and_157_out);
  nor nor_442 (nor_442_out, nor_426_out, or_24_out, nor_443_out);
  nor nor_443 (nor_443_out, nor_442_out, nor_427_out);
  nor nor_444 (nor_444_out, nor_428_out, or_24_out, nor_445_out);
  nor nor_445 (nor_445_out, nor_444_out, nor_429_out);
  nor nor_446 (nor_446_out, nor_430_out, or_24_out, nor_447_out);
  nor nor_447 (nor_447_out, nor_446_out, nor_431_out);
  nor nor_448 (nor_448_out, nor_432_out, or_24_out, nor_449_out);
  nor nor_449 (nor_449_out, nor_448_out, nor_433_out);
  nor nor_450 (nor_450_out, nor_434_out, or_24_out, nor_451_out);
  nor nor_451 (nor_451_out, nor_450_out, nor_435_out);
  nor nor_452 (nor_452_out, nor_436_out, or_24_out, nor_453_out);
  nor nor_453 (nor_453_out, nor_452_out, nor_437_out);
  nor nor_454 (nor_454_out, nor_438_out, or_24_out, nor_455_out);
  nor nor_455 (nor_455_out, nor_454_out, nor_439_out);
  nor nor_456 (nor_456_out, nor_440_out, or_24_out, nor_457_out);
  nor nor_457 (nor_457_out, nor_456_out, nor_441_out);
  and and_262 (and_262_out, nor_442_out, and_157_out);
  and and_263 (and_263_out, and_157_out, nor_443_out);
  and and_264 (and_264_out, nor_444_out, and_157_out);
  and and_265 (and_265_out, and_157_out, nor_445_out);
  and and_266 (and_266_out, nor_446_out, and_157_out);
  and and_267 (and_267_out, and_157_out, nor_447_out);
  and and_268 (and_268_out, nor_448_out, and_157_out);
  and and_269 (and_269_out, and_157_out, nor_449_out);
  and and_270 (and_270_out, nor_450_out, and_157_out);
  and and_271 (and_271_out, and_157_out, nor_451_out);
  and and_272 (and_272_out, nor_452_out, and_157_out);
  and and_273 (and_273_out, and_157_out, nor_453_out);
  and and_274 (and_274_out, nor_454_out, and_157_out);
  and and_275 (and_275_out, and_157_out, nor_455_out);
  and and_276 (and_276_out, nor_456_out, and_157_out);
  and and_277 (and_277_out, and_157_out, nor_457_out);
  nor nor_458 (nor_458_out, and_262_out, nor_459_out);
  nor nor_459 (nor_459_out, nor_458_out, or_24_out, and_263_out);
  nor nor_460 (nor_460_out, and_264_out, nor_461_out);
  nor nor_461 (nor_461_out, nor_460_out, or_24_out, and_265_out);
  nor nor_462 (nor_462_out, and_266_out, nor_463_out);
  nor nor_463 (nor_463_out, nor_462_out, or_24_out, and_267_out);
  nor nor_464 (nor_464_out, and_268_out, nor_465_out);
  nor nor_465 (nor_465_out, nor_464_out, or_24_out, and_269_out);
  nor nor_466 (nor_466_out, and_270_out, nor_467_out);
  nor nor_467 (nor_467_out, nor_466_out, or_24_out, and_271_out);
  nor nor_468 (nor_468_out, and_272_out, nor_469_out);
  nor nor_469 (nor_469_out, nor_468_out, or_24_out, and_273_out);
  nor nor_470 (nor_470_out, and_274_out, nor_471_out);
  nor nor_471 (nor_471_out, nor_470_out, or_24_out, and_275_out);
  nor nor_472 (nor_472_out, and_276_out, nor_473_out);
  nor nor_473 (nor_473_out, nor_472_out, or_24_out, and_277_out);
  and and_278 (and_278_out, STI_out, xnor_27_out);
  xnor xnor_27 (xnor_27_out, nor_458_out, STD_out);
  and and_279 (and_279_out, and_278_out, xnor_28_out);
  xnor xnor_28 (xnor_28_out, nor_460_out, STD_out);
  and and_280 (and_280_out, and_279_out, xnor_29_out);
  xnor xnor_29 (xnor_29_out, nor_462_out, STD_out);
  and and_281 (and_281_out, and_280_out, xnor_30_out);
  xnor xnor_30 (xnor_30_out, nor_464_out, STD_out);
  and and_282 (and_282_out, and_281_out, xnor_31_out);
  xnor xnor_31 (xnor_31_out, nor_466_out, STD_out);
  and and_283 (and_283_out, and_282_out, xnor_32_out);
  xnor xnor_32 (xnor_32_out, nor_468_out, STD_out);
  and and_284 (and_284_out, and_283_out, xnor_33_out);
  xnor xnor_33 (xnor_33_out, nor_470_out, STD_out);
  not not_8 (not_8_out, and_157_out);
  xnor xnor_34 (xnor_34_out, STI_out, nor_458_out);
  xnor xnor_35 (xnor_35_out, and_278_out, nor_460_out);
  xnor xnor_36 (xnor_36_out, and_279_out, nor_462_out);
  xnor xnor_37 (xnor_37_out, and_280_out, nor_464_out);
  xnor xnor_38 (xnor_38_out, and_281_out, nor_466_out);
  xnor xnor_39 (xnor_39_out, and_282_out, nor_468_out);
  xnor xnor_40 (xnor_40_out, and_283_out, nor_470_out);
  xnor xnor_41 (xnor_41_out, and_284_out, nor_472_out);
  nand OC_65 (OC_9_out[0], nor_458_out, STP_out);
  nand OC_66 (OC_9_out[1], nor_460_out, STP_out);
  nand OC_67 (OC_9_out[2], nor_462_out, STP_out);
  nand OC_68 (OC_9_out[3], nor_464_out, STP_out);
  nand OC_69 (OC_9_out[4], nor_466_out, STP_out);
  nand OC_70 (OC_9_out[5], nor_468_out, STP_out);
  nand OC_71 (OC_9_out[6], nor_470_out, STP_out);
  nand OC_72 (OC_9_out[7], nor_472_out, STP_out);
  or or_25 (or_25_out, WR_out, RD_out);
  Comparator #(.width(16)) comparator_1 (.a(16'hfeff), .b(OC_9_out), .eq(comparator_1_eq));  // open: gt, lt
  Comparator #(.width(16)) comparator_2 (.a(16'hfefe), .b(OC_9_out), .eq(comparator_2_eq));  // open: gt, lt
  and and_285 (and_285_out, nor_240_out, not_8_out);
  and and_286 (and_286_out, not_8_out, not_9_out, or_25_out);
  Button SFT_RST (.out(SFT_RST_out));
  Button HRD_RST (.out(HRD_RST_out));
  and and_287 (and_287_out, comparator_1_eq, WR_out);
  and and_288 (and_288_out, comparator_2_eq, RD_out);
  ROM #(.addrWidth(16)) rom_1 (
    .addr(OC_9_out), .data({in_9, in_8, in_6, in_5, in_4, in_3, in_2, in_1}), .sel(and_285_out));
  RAM #(.addrWidth(16), .bus("asynch")) ram_1 (
    .addr(OC_9_out), .data({in_9, in_8, in_6, in_5, in_4, in_3, in_2, in_1}), .sel(and_286_out), .ld(RD_out),
    .clr(in_7));
  TTY #(.rows(32), .cols(100)) tty_1 (
    .data({in_8, in_6, in_5, in_4, in_3, in_2, in_1}), .clk(not_8_out), .we(and_287_out), .clr(or_24_out));
  not not_9 (not_9_out, and_288_out);
  Keyboard #(.buflen(256)) keyboard_1 (
    .clk(and_157_out), .re(and_288_out), .clr(or_24_out), .avail(keyboard_1_data[7]),
    .data(keyboard_1_data[6:0]));
  assign {in_9, in_8, in_6, in_5, in_4, in_3, in_2, in_1} = and_288_out ? keyboard_1_data : 8'bz;  // Controlled_Buffer controlled_buffer_1

  // Notes on the sheet:
  //   OC drives only 0 and floats otherwise
  //   OC_2 drives only 0 and floats otherwise
  //   OC_3 drives only 0 and floats otherwise
  //   OC_4 drives only 0 and floats otherwise
  //   OC_5 drives only 0 and floats otherwise
  //   OC_6 drives only 0 and floats otherwise
  //   OC_7 drives only 0 and floats otherwise
  //   OC_8 drives only 0 and floats otherwise
  //   OC_9 drives only 0 and floats otherwise
  //   OC_10 drives only 0 and floats otherwise
  //   OC_11 drives only 0 and floats otherwise
  //   OC_12 drives only 0 and floats otherwise
  //   OC_13 drives only 0 and floats otherwise
  //   OC_14 drives only 0 and floats otherwise
  //   OC_15 drives only 0 and floats otherwise
  //   OC_16 drives only 0 and floats otherwise
  //   OC_17 drives only 0 and floats otherwise
  //   OC_18 drives only 0 and floats otherwise
  //   OC_19 drives only 0 and floats otherwise
  //   OC_20 drives only 0 and floats otherwise
  //   OC_21 drives only 0 and floats otherwise
  //   OC_22 drives only 0 and floats otherwise
  //   OC_23 drives only 0 and floats otherwise
  //   OC_24 drives only 0 and floats otherwise
  //   OC_25 drives only 0 and floats otherwise
  //   OC_26 drives only 0 and floats otherwise
  //   OC_27 drives only 0 and floats otherwise
  //   OC_28 drives only 0 and floats otherwise
  //   OC_29 drives only 0 and floats otherwise
  //   OC_30 drives only 0 and floats otherwise
  //   OC_31 drives only 0 and floats otherwise
  //   OC_32 drives only 0 and floats otherwise
  //   OC_33 drives only 0 and floats otherwise
  //   OC_34 drives only 0 and floats otherwise
  //   OC_35 drives only 0 and floats otherwise
  //   OC_36 drives only 0 and floats otherwise
  //   OC_37 drives only 0 and floats otherwise
  //   OC_38 drives only 0 and floats otherwise
  //   OC_39 drives only 0 and floats otherwise
  //   OC_40 drives only 0 and floats otherwise
  //   OC_41 drives only 0 and floats otherwise
  //   OC_42 drives only 0 and floats otherwise
  //   OC_43 drives only 0 and floats otherwise
  //   OC_44 drives only 0 and floats otherwise
  //   OC_45 drives only 0 and floats otherwise
  //   OC_46 drives only 0 and floats otherwise
  //   OC_47 drives only 0 and floats otherwise
  //   OC_48 drives only 0 and floats otherwise
  //   OC_49 drives only 0 and floats otherwise
  //   OC_50 drives only 0 and floats otherwise
  //   OC_51 drives only 0 and floats otherwise
  //   OC_52 drives only 0 and floats otherwise
  //   OC_53 drives only 0 and floats otherwise
  //   OC_54 drives only 0 and floats otherwise
  //   OC_55 drives only 0 and floats otherwise
  //   OC_56 drives only 0 and floats otherwise
  //   OC_57 drives only 0 and floats otherwise
  //   OC_58 drives only 0 and floats otherwise
  //   OC_59 drives only 0 and floats otherwise
  //   OC_60 drives only 0 and floats otherwise
  //   OC_61 drives only 0 and floats otherwise
  //   OC_62 drives only 0 and floats otherwise
  //   OC_63 drives only 0 and floats otherwise
  //   OC_64 drives only 0 and floats otherwise
  //   OC_65 drives only 0 and floats otherwise
  //   OC_66 drives only 0 and floats otherwise
  //   OC_67 drives only 0 and floats otherwise
  //   OC_68 drives only 0 and floats otherwise
  //   OC_69 drives only 0 and floats otherwise
  //   OC_70 drives only 0 and floats otherwise
  //   OC_71 drives only 0 and floats otherwise
  //   OC_72 drives only 0 and floats otherwise
  //   contents of rom_1 (hex, n*v repeats v):
  //   50 10 0 70 12 0 50 11 0 70 13 0 d0 14 0 ff 42 0 0 0 50 12 0 70 21 0 50 13 0 70 22 0 50 0 0 30 0 c2
  //   29 0 e0 70 ff fe 50 12 0 30 1 70 12 0 c1 3f 0 50 13 0 30 1 70 13 0 a0 14 0 22 48 65 6c 6c 6f 20 57
  //   6f 72 6c 64 21 22 a 0 6f 20 57 6f 72 6c 64 21 22 a
endmodule
